// Digital circuit Projects.dig as structural Verilog
module Projects (
  input  A2,
  input  A1,
  input  A0,
  input  F2,
  input  F1,
  input  F0,
  input  B1,
  input  B2,
  input  B0,
  output Q,
  output Cout
);

  wire and_1_out, and_2_out, and_4_out, FA_c_o, FA_s, FS_c_o, FS_s, multiplexer_2_out, not_1_out;

  and and_1 (and_1_out, A2, B2);
  and and_2 (and_2_out, A1, B1);
  and and_3 (and_2_out, A0, B0);
  Sub FS (.a(and_1_out), .b(and_2_out), .c_i(and_2_out), .s(FS_s), .c_o(FS_c_o));
  Add FA (.a(and_1_out), .b(and_2_out), .c_i(and_2_out), .s(FA_s), .c_o(FA_c_o));
  and and_4 (and_4_out, and_2_out, and_1_out);
  Multiplexer multiplexer_1 (.sel(F2), .in_0(FA_c_o), .in_1(FS_c_o), .out(Cout));
  Multiplexer multiplexer_2 (.sel(F2), .in_0(FA_s), .in_1(FS_s), .out(multiplexer_2_out));
  not not_1 (not_1_out, and_1_out);
  Multiplexer #(.Selector_Bits(2)) multiplexer_3 (
    .sel({F1, F0}), .in_0(multiplexer_2_out), .in_1(and_4_out), .in_2(and_1_out), .in_3(not_1_out), .out(Q));
endmodule
