// Digital circuit TASKCIRCUIT1.dig as structural Verilog
module TASKCIRCUIT1 (
  input  A,
  input  B,
  output XOR
);

  wire and_1_out, and_2_out, not_1_out, not_2_out;

  not not_1 (not_1_out, A);
  and and_1 (and_1_out, not_1_out, B);
  not not_2 (not_2_out, B);
  and and_2 (and_2_out, not_2_out, A);
  or or_1 (XOR, and_1_out, and_2_out);
endmodule
