// Digital circuit PROJECT.dig as structural Verilog
module PROJECT (
  input  A,
  input  B,
  input  C,
  input  F2,
  input  F1,
  input  F0,
  output Q,
  output Cout
);

  wire and_1_out, FA_c_o, FA_s, FS_c_o, FS_s, multiplexer_2_out, not_1_out;

  Sub FS (.a(A), .b(B), .c_i(C), .s(FS_s), .c_o(FS_c_o));
  Add FA (.a(A), .b(B), .c_i(C), .s(FA_s), .c_o(FA_c_o));
  and and_1 (and_1_out, B, A);
  Multiplexer multiplexer_1 (.sel(F2), .in_0(FA_c_o), .in_1(FS_c_o), .out(Cout));
  Multiplexer multiplexer_2 (.sel(F2), .in_0(FA_s), .in_1(FS_s), .out(multiplexer_2_out));
  not not_1 (not_1_out, A);
  Multiplexer #(.Selector_Bits(2)) multiplexer_3 (
    .sel({F1, F0}), .in_0(multiplexer_2_out), .in_1(and_1_out), .in_2(A), .in_3(not_1_out), .out(Q));
endmodule
