// Digital circuit PROJECT4.dig as structural Verilog
module PROJECT4 (
  input  F2,
  input  F1,
  input  F0,
  input  A0,
  input  B0,
  input  A1,
  input  B1,
  input  B2,
  input  A2,
  input  CIn,
  input  A3,
  input  B3,
  output Q0,
  output Q1,
  output Q2,
  output Q3,
  output Cout
);

  wire project_1_cout, project_2_cout, project_3_cout;

  PROJECT project_1 (.A(A0), .B(B0), .C(CIn), .F2(F2), .F1(F1), .F0(F0), .Q(Q0), .Cout(project_1_cout));
  PROJECT project_2 (.A(A1), .B(B1), .C(project_1_cout), .F2(F2), .F1(F1), .F0(F0), .Q(Q1), .Cout(project_2_cout));
  PROJECT project_3 (.A(A2), .B(B2), .C(project_2_cout), .F2(F2), .F1(F1), .F0(F0), .Q(Q2), .Cout(project_3_cout));
  PROJECT project_4 (.A(A3), .B(B3), .C(project_3_cout), .F2(F2), .F1(F1), .F0(F0), .Q(Q3), .Cout(Cout));
endmodule
