// Digital circuit Projects16.dig as structural Verilog
module Projects16 (
  input  Cin,
  input  F0,
  input  F1,
  input  F2,
  input  A1,
  input  A2,
  input  A3,
  input  A0,
  input  B0,
  input  B1,
  input  B2,
  input  B3,
  input  A5,
  input  A6,
  input  A7,
  input  A4,
  input  B4,
  input  B5,
  input  B6,
  input  B7,
  input  A8,
  input  A9,
  input  A10,
  input  A11,
  input  B8,
  input  B9,
  input  B10,
  input  B11,
  input  A12,
  input  A13,
  input  A14,
  input  A15,
  input  B12,
  input  B13,
  input  B14,
  input  B15,
  output Q0,
  output Q1,
  output Q2,
  output Q3,
  output Q4,
  output Q5,
  output Q6,
  output Q7,
  output Q8,
  output Q9,
  output Q10,
  output Q11,
  output Q12,
  output Q13,
  output Q14,
  output Q15,
  output Cout
);

  wire project4_1_cout, project4_2_cout, project4_3_cout;

  PROJECT4 project4_1 (
    .F2(F2), .F1(F1), .F0(F0), .A0(A0), .B0(B0), .A1(A1), .B1(B1), .B2(B2), .A2(A2), .CIn(Cin), .A3(A3),
    .B3(B3), .Q0(Q0), .Q1(Q1), .Q2(Q2), .Q3(Q3), .Cout(project4_1_cout));
  PROJECT4 project4_2 (
    .F2(F2), .F1(F1), .F0(F0), .A0(A4), .B0(B4), .A1(A5), .B1(B5), .B2(B6), .A2(A6), .CIn(project4_1_cout),
    .A3(A7), .B3(B7), .Q0(Q4), .Q1(Q5), .Q2(Q6), .Q3(Q7), .Cout(project4_2_cout));
  PROJECT4 project4_3 (
    .F2(F2), .F1(F1), .F0(F0), .A0(A8), .B0(B8), .A1(A9), .B1(B9), .B2(B10), .A2(A10), .CIn(project4_2_cout),
    .A3(A11), .B3(B11), .Q0(Q8), .Q1(Q9), .Q2(Q10), .Q3(Q11), .Cout(project4_3_cout));
  PROJECT4 project4_4 (
    .F2(F2), .F1(F1), .F0(F0), .A0(A12), .B0(B12), .A1(A13), .B1(B13), .B2(B14), .A2(A14),
    .CIn(project4_3_cout), .A3(A15), .B3(B15), .Q0(Q12), .Q1(Q13), .Q2(Q14), .Q3(Q15), .Cout(Cout));
endmodule
