// Digital circuit lab07.dig as structural Verilog
module lab07 (
  input  A,
  input  B,
  input  C,
  output Sum,
  output Cout
);

  wire and_1_out, and_2_out, not_1_out, not_2_out, xor_1_out;

  not not_1 (not_1_out, A);
  xor xor_1 (xor_1_out, A, B);
  and and_1 (and_1_out, B, not_1_out);
  not not_2 (not_2_out, xor_1_out);
  and and_2 (and_2_out, not_2_out, C);
  xor xor_2 (Sum, xor_1_out, C);
  or or_1 (Cout, and_2_out, and_1_out);
endmodule

/* Test case Sum:
A B C Sum
0 0 0 0
0 0 1 1
0 1 0 1
0 1 1 0
1 0 0 1
1 0 1 0
1 1 0 0
1 1 1 1
*/

/* Test case Cout:
A B C Cout
0 0 0 0
0 0 1 1
0 1 0 1
0 1 1 1
1 0 0 0
1 0 1 0
1 1 0 0
1 1 1 1
*/
