// Digital circuit mulplexer.dig as structural Verilog
module mulplexer (
  input  I0,
  input  I1,
  input  I2,
  input  I3,
  input  S1,
  input  S0,
  output Z
);

  wire and_1_out, and_2_out, and_3_out, and_4_out, not_1_out, not_2_out, not_3_out, not_4_out;

  not not_1 (not_1_out, S1);
  not not_2 (not_2_out, S0);
  not not_3 (not_3_out, S1);
  not not_4 (not_4_out, S0);
  and and_1 (and_1_out, I0, not_1_out, not_2_out);
  and and_2 (and_2_out, I1, not_3_out, S0);
  and and_3 (and_3_out, I2, not_4_out, S1);
  and and_4 (and_4_out, I3, S1, S0);
  or or_1 (Z, and_1_out, and_2_out, and_3_out, and_4_out);
endmodule
