// Digital circuit mult.dig as structural Verilog
module mult (
  input  X,
  input  Y,
  output Z
);

  wire and_1_out, and_3_out, not_1_out, not_2_out;

  not not_1 (not_1_out, X);
  not not_2 (not_2_out, Y);
  and and_1 (and_1_out, not_1_out, Y);
  and and_2 (and_1_out, X, not_2_out);
  and and_3 (and_3_out, X, Y);
  or or_1 (Z, and_1_out, and_3_out);
endmodule
